# Fritzing sketch Alohomora-3FA_Schematic_Fritzing (saved by Fritzing 0.9.3b)
breadboards: 1
perfboards: 3

parts:
  Componente1 = Arduino Nano (Rev3.0) (ICSP)  # not connected
  Componente2 = RFID-RC522-v2  # not connected
  J1 = Basic Servo  # not connected
  R1 = Resistor [tolerance=±5% resistance=330 package=THT]
  LED1 = LED - 5mm [color="Red (633nm)" package="5 mm [THT]"]
  J2 = Piezo Speaker  # not connected
  Power_plug1 = Power plug  # not connected
  J3 = Screw terminal - 2 pins [package=THT]  # not connected
  KEYPAD1 = Membrane Matrix Keypad  # not connected
  U1 = NodeMCU V3.0  # not connected
  J6 = Screw terminal - 2 pins [package=THT]
  J7 = Screw terminal - 2 pins [package=THT]
  F1 = FUSE [package=fuse_5mm]
  JP1 = Header 1 [package=1x01_offset]
  JP2 = Header 1 [package=1x01_offset]
  JP3 = Header 1 [package=1x01_offset]  # not connected
  JP4 = Header 1 [package=1x01_offset]
  D3 = Rectifier Diode [part_number=1N4007 package="300 mil [THT]"]
  D4 = Rectifier Diode [part_number=1N4001 package="300 mil [THT]"]
  U4 = RELAY-2 [package=relay-g5v]
  J8 = screw terminal, 6 pins
  J9 = screw terminal, 6 pins
  C1 = Electrolytic Capacitor [capacitance=1µF package="100 mil [THT, electrolytic]"]
  JP5 = Header 1 [package=1x01_offset]
  JP10 = Header 1 [package=1x01_offset]
  R2 = Resistor [tolerance=±5% resistance=330 package=THT]
  LED2 = LED - 5mm [color="Red (633nm)" package="5 mm [THT]"]
  J11 = Screw terminal - 2 pins [package=THT]
  J12 = Screw terminal - 2 pins [package=THT]
  F2 = FUSE [package=fuse_5mm]
  JP11 = Header 1 [package=1x01_offset]
  JP12 = Header 1 [package=1x01_offset]
  JP13 = Header 1 [package=1x01_offset]
  JP14 = Header 1 [package=1x01_offset]  # not connected
  JP15 = Header 1 [package=1x01_offset]
  JP16 = Header 1 [package=1x01_offset]
  D5 = Rectifier Diode [part_number=1N4007 package="300 mil [THT]"]
  D6 = Rectifier Diode [part_number=1N4001 package="300 mil [THT]"]
  U5 = RELAY-2 [package=relay-g5v]
  J13 = screw terminal, 6 pins
  J14 = screw terminal, 6 pins
  C2 = Electrolytic Capacitor [capacitance=1µF package="100 mil [THT, electrolytic]"]
  J15 = Screw terminal - 2 pins [package=THT]
  J16 = Screw terminal - 2 pins [package=THT]
  U6 = V_REG_LD1117VXX [package=78xxl]
  C3 = Electrolytic Capacitor [capacitance=10µF voltage=16V package="100 mil [THT, electrolytic]"]
  C4 = Electrolytic Capacitor [capacitance=22µF package="100 mil [THT, electrolytic]"]
  C5 = Ceramic Capacitor [capacitance=100nF package="100 mil [THT, multilayer]"]

nets:
  N1: R1.Pin_0, JP1.1, U4.10, J9.pin1, J9.pin6, C1.+
  N2: R1.Pin_1, LED1.anode
  N3: LED1.cathode, U4.1, J8.pin6, C1.-, JP5.1
  N4: J6.pin1, J7.pin2
  N5: J6.pin2, F1.1, JP4.1
  N6: J7.pin1, JP2.1, D3.anode, U4.2, U4.5
  N7: D3.cathode, D4.cathode, U4.6, U4.9, JP10.1
  N8: J8.pin1, J8.pin2
  N9: R2.Pin_0, JP11.1, U5.10, J14.pin1, J14.pin6, C2.+
  N10: R2.Pin_1, LED2.anode
  N11: LED2.cathode, JP15.1, U5.1, J13.pin6, C2.-
  N12: J11.pin1, JP16.1, D5.anode, U5.2, U5.5
  N13: J11.pin2, J12.pin1
  N14: J12.pin2, F2.1, JP12.1
  N15: JP13.1, D5.cathode, D6.cathode, U5.6, U5.9
  N16: J13.pin1, J13.pin2
  N17: J15.pin1, U6.GND, C3.+
  N18: J15.pin2, J16.pin1
  N19: J16.pin2, U6.IN, C4.+, C5.0

notes:
  +
  -
  INPUT 12 volt
  12 Volt - Voltage divider
  Switch
  On-Off
  OUT +12V
  OUT - ground
  By-Pass
  3.3 Volt - Voltage divider
  OUT +3.3V
  INPUT 3.3 volt
  1117-3,3
  5 to 3,3 Volt - step down

custom parts:
  RFID-RC522-v2: A simple China made RFID-RC522 Reader; do check the pin labels, as this is a MFRC522 based clone.
  Membrane Matrix Keypad: Membrane Matrix 3x4 Keypad
  NodeMCU V3.0: ESP8266 based NodeMCU
